# Fritzing sketch Esquema0 (saved by Fritzing 0.9.10b)
breadboards: 1

parts:
  R3 = Rotary Potentiometer (Large) [maximum_resistance=100kΩ knob_status=50% power=0.5W package=THT]
  R4 = Rotary Potentiometer (Large) [maximum_resistance=100kΩ knob_status=50% power=0.5W package=THT]
  R5 = Rotary Potentiometer (Large) [maximum_resistance=100kΩ knob_status=50% power=0.5W package=THT]
  R6 = Rotary Potentiometer (Large) [maximum_resistance=100kΩ knob_status=50% power=0.5W package=THT]
  Componente1 = Arduino Uno (Rev3)

nets:
  N1: R3.leg1, R4.leg1, R5.leg1, R6.leg1, Componente1.5V
  N2: R3.wiper, Componente1.A1
  N3: R3.leg2, R4.leg2, R5.leg2, R6.leg2, Componente1.GND
  N4: R5.wiper, Componente1.A3
  N5: R6.wiper, Componente1.A2

notes:
  Cables:
  Rosa: Datos
  Negro: GND (Tierra)
  Rojo: 5V (Voltaje)
